# Fritzing sketch CapacimetrINO (saved by Fritzing 0.9.3b)
breadboards: 1

parts:
  C1 = Electrolytic Capacitor [capacitance=1µF package="100 mil [THT, electrolytic]"]
  Componente1 = Arduino Uno (Rev3)
  ZS-042_RTC1 = ZS-042 RTC Module
  LCD1 = LCD screen  # not connected

nets:
  N1: C1.-, Componente1.A1
  N2: C1.+, Componente1.A0
  N3: Componente1.A4/SDA, ZS-042_RTC1.SDA
  N4: Componente1.A5/SCL, ZS-042_RTC1.SCL
  5V: Componente1.5V, ZS-042_RTC1.VCC
  GND: Componente1.GND, ZS-042_RTC1.GND

notes:
  Condensatore da misurare
  Progetti & Tutorial Arduino!
